# Fritzing sketch interfacingwithdht22 (saved by Fritzing 0.9.6b)

parts:
  DHT1 = DHT22 Humidity and Temperature Sensor
  U1 = LuaNode32 / ESP32

nets:
  VDD: DHT1.VDD, U1.3V3
  N1: DHT1.DATA, U1.D2
  GND: DHT1.GND, U1.GND

notes:
  3.3/5v vcc
  3.3v
  GND
  Data
  DHT22
  ESP32

custom parts:
  LuaNode32 / ESP32: ESP32 based LuaNode32
