# Fritzing sketch mushroomFarm (saved by Fritzing 0.9.6b)

parts:
  U1 = LuaNode32 / ESP32
  U2 = Module 4 Relais 5V [package="Module 4 Relais 5V"]
  DHT1 = DHT22 Humidity and Temperature Sensor
  Power_plug1 = Power plug
  Part1 = Lilypad Battery Connect
  F1 = Fan - Ventilador [package=THT]
  LED1 = LEDs [package=led10mm]
  F2 = Fan - Ventilador [package=THT]
  LED2 = LEDs [package=led10mm]

nets:
  GND: U1.GND, U2.GND, DHT1.GND, Power_plug1.GND
  VCC: U1.Vin, U2.VCC, DHT1.VDD, Power_plug1.VCC
  N1: U1.D2, DHT1.DATA
  N2: U1.D4, U2.IN4
  N3: U1.D5, U2.IN3
  N4: U1.D18, U2.IN2
  N5: U1.D19, U2.IN1
  N6: U2.K1-NF, U2.K2-NF, U2.K3-NF, U2.K4-NF, Part1.-
  N7: U2.K1-NO, LED1.C
  N8: U2.K2-NO, LED2.C
  N9: U2.K3-NO, F2.GND
  N10: U2.K4-NO, F1.GND
  5V: Part1.+, F1.5V, LED1.A, F2.5V, LED2.A

notes:
  Humidifier*
  Light
  Cooler
  Heater
  DHT22
  AC 240V
  DC 5V
  4-Channel Relay Module
  ESP32

custom parts:
  LuaNode32 / ESP32: ESP32 based LuaNode32
  Module 4 Relais 5V: Module 4 Relais 5V 4x SPD-06VDC-SD-C
  Fan - Ventilador: Ventilador de 2 pines, se encuentra comunmente en computadoras de escritorio
  LEDs: LEDs Standard schematic elements and footprints for 5mm, 3mm, 1206, and 0603 sized LEDs. 5mm - Spark Fun Electronics SKU : COM-00529 (and others)
